// Logisim project 7_seg_display.circ as structural Verilog: 1 circuit, main circuit main
module main (
  input  in_1
);

  wire not_1_out;

  not not_1 (not_1_out, in_1);
  _7_Segment_Display u_7_segment_display_1 (
    .g(not_1_out), .a(not_1_out), .b(not_1_out), .e(not_1_out), .d(not_1_out));  // open: f, c, dp
  _7_Segment_Display u_7_segment_display_2 (.g(in_1), .a(in_1), .b(in_1), .e(in_1), .d(in_1));  // open: f, c, dp

  // Notes on the sheet:
  //   ID 41220300622
  //   2nd Last Digit
  //   Last Digit
endmodule
